# Fritzing sketch wiring (saved by Fritzing 1.0.4)
breadboards: 1

parts:
  BATT1 = LiPoly Battery (1300mAh)
  BATT2 = LiPoly Battery (1300mAh)
  BATT3 = LiPoly Battery (1300mAh)
  A1 = drv-1012
  A2 = drv-1012
  3_3V = mini560 [part_number=Mini560 package=SMD]
  5V = mini560 [part_number=Mini560 package=SMD]
  S1 = Toggle Switch spst [package=THT]
  M1 = DOIT Esp32 DevKit v1 (30 pins long, 11 pins width) [part_number=ESP32S-PIN30]
  Part1 = Adafruit VL53L1X [part_number="Adafruit #3967"]
  Part2 = Adafruit VL53L1X [part_number="Adafruit #3967"]
  Part3 = Adafruit VL53L1X [part_number="Adafruit #3967"]
  Part4 = Adafruit VL53L1X [part_number="Adafruit #3967"]
  TTP223B1 = TTP223B Capacitive Touch Sensor Module
  Part5 = Adafruit LSM6DS33 6-DoF Accel + Gyro IMU [part_number="Adafruit #4480"]
  TCRT1 = TCRT5000 sensor module [part_number=151608]
  TCRT3 = TCRT5000 sensor module [part_number=151608]
  TCRT4 = TCRT5000 sensor module [part_number=151608]
  TCRT5 = TCRT5000 sensor module [part_number=151608]
  TCRT6 = TCRT5000 sensor module [part_number=151608]
  Grove1 = Grove OLED 128x96
  M2 = gear-motor
  M3 = gear-motor
  C24 = Ceramic Capacitor [capacitance=0.22µF voltage=35V package="100 mil [THT, multilayer]"]  # not connected
  C25 = Ceramic Capacitor [capacitance=0.22µF voltage=35V package="100 mil [THT, multilayer]"]  # not connected
  C12 = Ceramic Capacitor [capacitance=0.1µF voltage=35V package="100 mil [THT, multilayer]"]
  Part6 = Adafruit VL53L1X [part_number="Adafruit #3967"]
  C13 = Ceramic Capacitor [capacitance=0.1µF voltage=35V package="100 mil [THT, multilayer]"]
  C14 = Ceramic Capacitor [capacitance=0.1µF voltage=35V package="100 mil [THT, multilayer]"]
  C15 = Ceramic Capacitor [capacitance=0.1µF voltage=35V package="100 mil [THT, multilayer]"]
  C16 = Ceramic Capacitor [capacitance=0.1µF voltage=35V package="100 mil [THT, multilayer]"]
  C1 = Electrolytic Capacitor [capacitance=1mF voltage=35V package="100 mil [THT, electrolytic]"]
  C2 = Electrolytic Capacitor [capacitance=1mF voltage=35V package="100 mil [THT, electrolytic]"]
  R1 = Resistor [tolerance=±0.05% power=0.5W resistance=2.2k package=THT]
  R2 = Resistor [tolerance=±0.05% power=0.5W resistance=2.2k package=THT]
  C27 = Ceramic Capacitor [capacitance=100nF voltage=35V package="100 mil [THT, multilayer]"]
  C28 = Ceramic Capacitor [capacitance=100nF voltage=35V package="100 mil [THT, multilayer]"]
  C29 = Ceramic Capacitor [capacitance=100nF voltage=35V package="100 mil [THT, multilayer]"]
  C30 = Ceramic Capacitor [capacitance=100nF voltage=35V package="100 mil [THT, multilayer]"]
  C31 = Ceramic Capacitor [capacitance=100nF voltage=35V package="100 mil [THT, multilayer]"]
  C32 = Ceramic Capacitor [capacitance=0.1µF voltage=35V package="100 mil [THT, multilayer]"]

nets:
  N1: BATT1.positive, A1.Pin_12, A2.Pin_12, S1.L1, S1.COM, C1.+, C2.+
  N2: BATT1.negative, BATT2.positive
  N3: BATT2.negative, BATT3.positive
  N4: BATT3.negative, A1.Pin_11, A2.Pin_11
  N5: A1.Pin_1, A2.Pin_1, 3_3V.pin_3, 3_3V.pin_4, 3_3V.pin_6, 3_3V.pin_7, 5V.pin_3, 5V.pin_4, 5V.pin_7, M1.GND, C1.-, C2.-
  N6: A1.Pin_3, A1.Pin_5, A1.Pin_7, A2.Pin_3, A2.Pin_5, A2.Pin_7, 5V.pin_8, 5V.pin_9, M1.VIN, R1.Pin_0, R2.Pin_0
  N7: A1.Pin_4, M1.D19
  N8: A1.Pin_8, M1.D18
  N9: A1.Pin_9, M3.pin_2
  N10: A1.Pin_10, M3.pin_1
  N11: A2.Pin_4, M1.D22
  N12: A2.Pin_8, M1.D21
  N13: A2.Pin_9, M2.pin_2
  N14: A2.Pin_10, M2.pin_1
  N15: 3_3V.pin_1, 3_3V.pin_2, 5V.pin_1, 5V.pin_2
  N16: 3_3V.pin_8, 3_3V.pin_9, TTP223B1.VCC
  N17: M1.D4, TTP223B1.SIG
  N18: M1.RX2, Part6.XSHUT
  N19: M1.TX2, Part1.XSHUT
  N20: M1.D5, Grove1.SCL
  N21: M1.D23, Grove1.SDA
  N22: M1.VN, TCRT6.D+
  N23: M1.D34, TCRT5.D+
  N24: M1.D35, TCRT4.D+
  N25: M1.D32, TCRT3.D+
  N26: M1.D33, TCRT1.D+
  N27: M1.D25, Part1.SCL, Part2.SCL, Part3.SCL, Part4.SCL, Part5.SCL, Part6.SCL, R2.Pin_1
  N28: M1.D26, Part1.SDA, Part2.SDA, Part3.SDA, Part4.SDA, Part5.SDA, Part6.SDA, R1.Pin_1
  N29: M1.D27, Part3.XSHUT
  N30: M1.D14, Part4.XSHUT
  N31: M1.D13, Part2.XSHUT
  GND: Part1.GND, Part2.GND, Part3.GND, Part4.GND, TTP223B1.GND, Part5.GND, TCRT1.T+, TCRT3.T+, TCRT4.T+, TCRT5.T+, TCRT6.T+, Grove1.GND, C12.0, Part6.GND, C13.0, C14.0, C15.0, C16.0, C27.0, C28.0, C29.0, C30.0, C31.0, C32.0
  VCC: Part1.VCC, Part2.VCC, Part3.VCC, Part4.VCC, Part5.VCC, C12.1, Part6.VCC, C13.1, C14.1, C15.1, C16.1, C32.1
  N32: TCRT1.T-, TCRT3.T-, TCRT4.T-, TCRT5.T-, TCRT6.T-, Grove1.VCC, C27.1, C28.1, C29.1, C30.1, C31.1

custom parts:
  LiPoly Battery (1300mAh): Lithium Ion Polymer Battery (1300mAh)
  drv-1012: .The BTS7960 is a fully integrated high current H bridge module for motor drive applications.
  mini560: 5A DC-DC Mini 560 Step Down Stabilized Voltage Supply Module Output 3.3 5V 9V 12V Step-down Power Converter Board Module. Oct 19 2025 Add SMD varient vanepp.
  mini560: 5A DC-DC Mini 560 Step Down Stabilized Voltage Supply Module Output 3.3 5V 9V 12V Step-down Power Converter Board Module. Oct 19 2025 Add SMD varient vanepp.
  Toggle Switch spst: Toggle Switch single pole single throw
  DOIT Esp32 DevKit v1 (30 pins long, 11 pins width): The DOIT Esp32 DevKit v1 is one of the development board created by DOIT to evaluate the ESP-WROOM-32 module. It is based on the ESP32 microcontroller that boasts Wifi, Bluetooth, Ethernet and Low Power support all in a single chip. (vanepp) made breadboard work, adjusted pin numbering and labels and reduced size of schematic and cleaned up pcb. This chip is 30pins long (2 x15) and 11 pins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
  Adafruit VL53L1X: The Adafruit VL53L1X Time of Flight Distance Sensor (also known as VL53L1CX) is a Time of Flight distance sensor that has a massive 4 meter range and LIDAR-like precision. The sensor contains a very tiny invisible laser source and a matching sensor. The VL53L1X can detect the "time of flight", or how long the light has taken to bounce back to the sensor. Since it uses a very narrow light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
  TTP223B Capacitive Touch Sensor Module: The TTP223B capacitive touch sensor module uses the TTP223B IC. The appropriate voltage is approximately 2 to 5.5 volts.
  Adafruit LSM6DS33 6-DoF Accel + Gyro IMU: Add motion and orientation sensing to your Arduino project with this affordable 6 Degree of Freedom (6-DoF) sensor with sensors from ST. The board includes an LSM6DS33, a 6-DoF IMU accelerometer + gyro. The 3-axis accelerometer, can tell you which direction is down towards the Earth (by measuring gravity) or how fast the board is accelerating in 3D space. The 3-axis gyroscope that can measure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
  TCRT5000 sensor module: breakout board with TCRT5000

// code stored in the sketch: Untitled3.ino

